# Fritzing sketch PoolPump (saved by Fritzing 0.9.3b)
circuit board: 8.46667cm x 5.64444cm
breadboards: 1

parts:
  part = NPN-Transistor [part_number=PN2222A package="TO92 [THT]"]
  R1 = Resistor [tolerance=±5% resistance=10k package=THT]
  Raspberry_Pi_Zero1 = Raspberry Pi Zero
  HAMLIN = DIP-Relay-D31A [part_number="HE721 A05-10 8018"]
  part_2 = AC Power [voltage=240V frequency=50]
  240VAC = 240VAC Relay [package=THT]
  POOLPUMP_240VAC = DC Motor
  On_/_Off_(ARM) = Taiway 100-SP-X-T1 SPDT Miniature Toggle Switch [part_number="Toggle Switch" package=THT]
  Run = Pushbutton [part_number="Pushbutton (Blue)" package="[THT]"]
  R2 = Resistor [tolerance=±5% resistance=1k package=THT]
  R3 = Resistor [tolerance=±5% resistance=10k package=THT]
  R4 = Resistor [tolerance=±5% resistance=1k package=THT]
  R5 = Resistor [tolerance=±5% resistance=10k package=THT]
  ON = LED - 5mm [color="Red (633nm)" package="5 mm [THT]"]
  R6 = Resistor [tolerance=±5% resistance=220 package=THT]
  ARMED = LED - 5mm [color="Orange (605nm)" package="5 mm [THT]"]
  R7 = Resistor [tolerance=±5% resistance=220 package=THT]
  RUNNING = LED - 5mm [color="Green (570nm)" package="5 mm [THT]"]
  R8 = Resistor [tolerance=±5% resistance=220 package=THT]

nets:
  GND: part.E, Raspberry_Pi_Zero1.GND, R3.Pin_0, R5.Pin_0
  N1: part.B, R1.Pin_1
  N2: part.C, HAMLIN.Coil2_-
  N3: R1.Pin_0, Raspberry_Pi_Zero1.GPIO24
  3V3: Raspberry_Pi_Zero1.3v3, Raspberry_Pi_Zero1.3V3, On_/_Off_(ARM).COM, Run.Pin_3, Run.Pin_4, ON.cathode, ARMED.cathode, RUNNING.cathode
  N4: Raspberry_Pi_Zero1.GPIO17, R6.Pin_1
  N5: Raspberry_Pi_Zero1.GPIO27, R7.Pin_1
  N6: Raspberry_Pi_Zero1.GPIO22, R8.Pin_1
  N7: Raspberry_Pi_Zero1.5V, HAMLIN.COIL1_+
  N8: HAMLIN.A1_Switch_Terminal_A, part_2.V-
  N9: HAMLIN.B2_Switch_Terminal_B, 240VAC.COIL1, 240VAC.C1, 240VAC.C2
  N10: part_2.V+, 240VAC.COIL2, POOLPUMP_240VAC.pin_2
  N11: 240VAC.A, POOLPUMP_240VAC.pin_1
  N12: On_/_Off_(ARM).L2, R4.Pin_1, R5.Pin_1
  N13: Run.Pin_1, Run.Pin_2, R2.Pin_1, R3.Pin_1
  N14: ON.anode, R6.Pin_0
  N15: ARMED.anode, R7.Pin_0
  N16: RUNNING.anode, R8.Pin_0
